# Fritzing sketch rover-V1 (saved by Fritzing 0.9.3b)

parts:
  Raspberry_Pi_1 = Raspberry Pi 3 [part_number=RPI-3-V1.2]
  Part1 = Arduino Pro Mini v13
  U1 = 74AHCT125 [part_number=SN74AHCT125 package=dil14]
  Motor_Controller = Header 4 [package=1x04-1mm-ra]
  Power_In = Header 3 [package=jst-3-smd]
  R1 = Resistor [tolerance=±5% resistance=220 package="2512 [SMD]"]
  R2 = Resistor [tolerance=±5% resistance=220 package="2512 [SMD]"]

nets:
  GND: Raspberry_Pi_1.GND, Part1.GND, U1.GND, Power_In.2, R2.Pin_1
  N1: Raspberry_Pi_1.GIPO15, Part1.D0/TX
  N2: Raspberry_Pi_1.GIPO14, Part1.D1/RX
  5V: Raspberry_Pi_1.5V, Part1.RAW, U1.VCC, Power_In.3
  N3: Part1.A0, R2.Pin_0
  N4: Part1.D9_PWM, U1.4A
  N5: Part1.D6_PWM, U1.1A
  N6: Part1.D5_PWM, U1.2A
  N7: Part1.D3_PWM, U1.3A
  N8: U1.1Y, Motor_Controller.1
  N9: U1.2Y, Motor_Controller.2
  N10: U1.3Y, Motor_Controller.3
  N11: U1.4Y, Motor_Controller.4
  N12: Power_In.1, R1.Pin_0

custom parts:
  74AHCT125: Quad Level-Shifter (3V to 5V) Quadruple Bus Buffer Gates With 3-State Outputs
